// Logisim project lab4part1.circ as structural Verilog: 1 circuit, main circuit main
module main (
  input  in_1,
  input  in_2,
  output Pin_6,
  output out_4
);

  wire C1_2_out, C1_out, C2_out;

  not C2 (C2_out, in_1);
  nand C1 (C1_out, in_1, in_2);
  nand C1_2 (C1_2_out, in_2, C2_out);
  nand C1_3 (Pin_6, C1_out, out_4);
  nand C1_4 (out_4, Pin_6, C1_2_out);

  // Notes on the sheet:
  //   Digital Board Pin#1
  //   Digital Board Pin#3
  //   Pin#1
  //   Pin#1
  //   Pin#2
  //   Pin#9
  //   Pin#10
  //   Pin#2
  //   Pin#3
  //   Pin#8
  //   Pin#4
  //   Pin#5
  //   Pin#12
  //   Pin#13
  //   Pin#11
  //   Digtal Board Pin#17
  //   Digtal Board Pin#19
endmodule
