// Logisim project Part1.circ as structural Verilog: 1 circuit, main circuit main
module main (
  input  x,
  input  s,
  input  y,
  output z
);

  wire C1_2_out, C1_out, not_1_out;

  not not_1 (not_1_out, s);
  and C1 (C1_out, x, not_1_out);
  and C1_2 (C1_2_out, s, y);
  or C2 (z, C1_out, C1_2_out);

  // Notes on the sheet:
  //   Digital Board
  //   PIN2
  //   Digital Board
  //   PIN1
  //   Digital Board
  //   PIN3
  //   C3
  //   PIN1
  //   PIN2
  //   74LS04 NOT
  //   PIN1
  //   PIN2
  //   PIN4
  //   PIN5
  //   74LS08 AND2
  //   PIN3
  //   PIN6
  //   74LS08 AND2
  //   PIN1
  //   PIN2
  //   PIN3
  //   74LS32 OR2
  //   Digital Board
  //   PIN17
endmodule
