// Logisim project Part2.1.circ as structural Verilog: 1 circuit, main circuit main
module main (
  input  a,
  input  b,
  input  c,
  output z
);

  wire and_1_out, not_1_out, not_2_out, or_1_out;

  not not_1 (not_1_out, b);
  or or_1 (or_1_out, a, b);
  and and_1 (and_1_out, not_1_out, c);
  not not_2 (not_2_out, or_1_out);
  or or_2 (z, not_2_out, and_1_out);

  // Notes on the sheet:
  //   Digital Board
  //   Pin1
  //   Digital Board
  //   Pin2
  //   Digital Board
  //   Pin3
  //   Pin1
  //   Pin1
  //   Pin2
  //   C3
  //   Pin2
  //   74LS04
  //   74LS32
  //   Pin3
  //   C1
  //   Pin3
  //   74LS08
  //   Pin1
  //   C2
  //   Pin2
  //   C3
  //   Pin4
  //   74LS04
  //   Pin3
  //   Pin4
  //   Pin5
  //   74LS32
  //   Pin6
  //   C1
  //   Digital Board
  //   Pin17
endmodule
