// Logisim project Part2.2.circ as structural Verilog: 1 circuit, main circuit main
module main (
  input  a,
  input  c,
  input  b,
  output z
);

  wire not_1_out, not_2_out, or_1_out;

  not not_1 (not_1_out, a);
  not not_2 (not_2_out, b);
  or or_1 (or_1_out, not_1_out, c);
  and and_1 (z, or_1_out, not_2_out);

  // Notes on the sheet:
  //   Digital Board
  //   Pin1
  //   Digital Board
  //   Pin3
  //   Digital Board
  //   Pin2
  //   C3
  //   Pin3
  //   74LS04
  //   C3
  //   Pin1
  //   74LS04
  //   Pin1
  //   Pin4
  //   Pin2
  //   Pin2
  //   74LS32
  //   Pin3
  //   C1
  //   Pin1
  //   Pin2
  //   74LS08
  //   Pin3
  //   C2
  //   Digital Board
  //   Pin17
endmodule
