// Logisim project part1.circ as structural Verilog: 1 circuit, main circuit main
module main (
  input  clock,
  input  enable,
  input  reset
);

  wire and_1_out, and_2_out, and_3_out, and_4_out, and_5_out, and_6_out, and_7_out, t_ff_1_q, t_ff_2_q,
       t_ff_3_q, t_ff_4_q, t_ff_5_q, t_ff_6_q, t_ff_7_q;

  T_Flip_Flop t_ff_1 (.clk(clock), .T(enable), .Q(t_ff_1_q), .reset(reset));  // open: Qn, preset, en
  and and_1 (and_1_out, t_ff_7_q, and_6_out);
  and and_2 (and_2_out, t_ff_1_q, enable);
  T_Flip_Flop t_ff_2 (.clk(clock), .T(and_1_out), .Q(t_ff_2_q), .reset(reset));  // open: Qn, preset, en
  T_Flip_Flop t_ff_3 (.clk(clock), .T(and_2_out), .Q(t_ff_3_q), .reset(reset));  // open: Qn, preset, en
  T_Flip_Flop t_ff_4 (.clk(clock), .T(and_3_out), .Q(t_ff_4_q), .reset(reset));  // open: Qn, preset, en
  and and_3 (and_3_out, t_ff_2_q, and_1_out);
  and and_4 (and_4_out, t_ff_3_q, and_2_out);
  and and_5 (and_5_out, t_ff_4_q, and_3_out);
  T_Flip_Flop t_ff_5 (.clk(clock), .T(and_4_out), .Q(t_ff_5_q), .reset(reset));  // open: Qn, preset, en
  T_Flip_Flop t_ff_6 (.clk(clock), .T(and_5_out), .Q(t_ff_6_q), .reset(reset));  // open: Qn, preset, en
  T_Flip_Flop t_ff_7 (.clk(clock), .T(and_6_out), .Q(t_ff_7_q), .reset(reset));  // open: Qn, preset, en
  and and_6 (and_6_out, t_ff_5_q, and_4_out);
  T_Flip_Flop t_ff_8 (.clk(clock), .T(and_7_out), .reset(reset));  // open: Q, Qn, preset, en
  and and_7 (and_7_out, t_ff_6_q, and_5_out);
endmodule
